// Digital circuit Capstone.dig as structural Verilog
module Capstone (
  input  V,
  input  L,
  input  clk,
  input  reset,
  output R,
  output F,
  output [2:0] State
);

  wire and_1_out, and_2_out, and_3_out, and_4_out, and_5_out, and_6_out, and_7_out, L_1, or_1_out, or_2_out,
       Q_0_t, Q_1_t, Q_2_t, V_2;

  not not_1 (V_2, V);
  not not_2 (L_1, L);
  and and_1 (and_1_out, Q_0_t, Q_1_t, L_1, V);
  and and_2 (and_2_out, Q_0_t, Q_2_t, L, V);
  and and_3 (and_3_out, L, V_2);
  and and_4 (and_4_out, F, Q_2_t, V);
  and and_5 (and_5_out, Q_0_t, Q_1_t, L, V);
  and and_6 (and_6_out, F, State[0], V);
  or or_1 (or_1_out, and_1_out, and_2_out);
  or or_2 (or_2_out, and_3_out, and_4_out, and_5_out);
  D_FF_AS d_ff_as_1 (.Set(1'b0), .D(and_6_out), .C(clk), .Clr(reset), .Q(State[2]), .nQ(Q_0_t));
  D_FF_AS d_ff_as_2 (.Set(1'b0), .D(or_1_out), .C(clk), .Clr(reset), .Q(F), .nQ(Q_1_t));
  D_FF_AS d_ff_as_3 (.Set(1'b0), .D(or_2_out), .C(clk), .Clr(reset), .Q(State[0]), .nQ(Q_2_t));
  and and_7 (and_7_out, V, L_1);
  or or_3 (R, and_7_out, State[2]);

  assign State[1] = F;

  // Other names for the same wires on the sheet: L_2 = L; Q_0 = State[2]; Q_1 = F; Q_2 = State[0]; V_1 = V
endmodule
